# Fritzing sketch RFLINK BME280 RXB6 ESP8266 (saved by Fritzing 0.9.3b)

parts:
  U3 = NodeMCU V1.0
  BME-280 = GY-BMEP280 Barometric Pressure Sensor - Breakout
  U4 = RF-LINK_RX [package=rf-link_rx]
  L1 = Inductor [package="400 mil [THT]"]

nets:
  N1: U3.D1, U4.DATA
  3V3: U3.3V3, BME-280.VCC
  GND: U3.GND, BME-280.GND, U4.GND
  N2: U3.D5, BME-280.SCL
  N3: U3.D6, BME-280.SDA
  VIN: U3.Vin, U4.+5V
  N4: U4.ANT, L1.pin_1

notes:
  MCUIOT
  BME-GD
  MCUIOT - BME-GD
  Garage Door Monitor

custom parts:
  NodeMCU V1.0: ESP8266 based NodeMCU
  GY-BMEP280 Barometric Pressure Sensor - Breakout: The BME280 is a chip which was originally designed for the next generation of smartphones. It is made up of a very accurate pressure sensor and an associated temperature sensor which helps calibrate the pressure readings. And just for fun they threw in a pretty solid humidity sensor in there as well! So with an I2C connection you have access to enough weather data to make some pretty good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
